# Fritzing sketch pzem_mqtt (saved by Fritzing 0.9.3b)

parts:
  U1 = ESP8266 WiFi Module [part_number=ESP8266]
  U2 = Molex Picoblade Series Header [part_number=0532610419 package=Picoblade-53261-0419]
  Power_plug1 = Power plug

nets:
  VCC: U1.VCC, U1.CH_PD, U2.1, Power_plug1.VCC
  N1: U1.GPIO_2, U2.2
  GND: U1.GND, U2.4, Power_plug1.GND
  N2: U1.TXD, U2.3

notes:
  +3.3V power
  PZEM-004t

custom parts:
  ESP8266 WiFi Module: Generic WiFi Module based on the ESP8266 with onboard PCB antenna and UART communications
