# Fritzing sketch scr_control_local (saved by Fritzing 0.9.3b)
breadboards: 1

parts:
  Part1 = Arduino Nano (Rev3.0)
  S1 = Momentary Switch [package=ksa_sealed_tac_switch]
  S2 = Momentary Switch [package=ksa_sealed_tac_switch]

nets:
  N1: Part1.D5, S2.4
  N2: Part1.D6, S1.4
  N3: S1.2, S2.2

notes:
  Goes to the input zero signal
  Goes to the output SCR signal
