# Fritzing sketch scr_control_remote (saved by Fritzing 0.9.3b)
breadboards: 1

parts:
  Part1 = Arduino Nano (Rev3.0)
  Part3 = NRF24L01+ Breakout Board

nets:
  GND: Part1.GND, Part3.GND
  N1: Part1.D9, Part3.CE
  N2: Part1.D10, Part3.CS
  N3: Part1.D11/MOSI, Part3.MOSI
  N4: Part1.D12/MISO, Part3.MISO
  3V3: Part1.3V3, Part3.VCC
  N5: Part1.D13/SCK, Part3.SCK

notes:
  Goes to the input zero signal
  Goes to the output SCR signal
